// Logisim project proc_RAM.circ as structural Verilog: 1 circuit, main circuit main
module main (
);

  wire and_3_out, and_4_out, and_6_out, and_7_out, Cl, code, comparator_1_eq, comparator_2_eq,
       comparator_3_lt, comparator_4_gt, comparator_5_lt, comparator_6_gt, CORD_select, data, data_ins_prime,
       demultiplexer_1_out0, demultiplexer_1_out1, demultiplexer_1_out2, demultiplexer_1_out3,
       demultiplexer_1_out4, demultiplexer_1_out5, demultiplexer_1_out6, demultiplexer_1_out7,
       demultiplexer_1_out8, demultiplexer_1_out9, demultiplexer_1_out10, demultiplexer_1_out11,
       demultiplexer_1_out12, demultiplexer_1_out13, demultiplexer_1_out14, demultiplexer_1_out15,
       DISPLAY_select, DOWN_button, hi, LEFT_button, lo, memory, not_1_out, not_2_out, not_3_out, not_6_out,
       or_1_out, or_2_out, or_3_out, or_4_out, read_write_prime, RIGHT_button, STOP_out, STOP_select,
       UP_button;
  wire [0:0] register_1_q;
  wire [3:0] column, Column_q, controlled_buffer_6_out, X_coord_q, Y_coord_q;
  wire [7:0] addr, cdm_8_mark5_1_p6, cdm_8_mark5_1_p7, D, ram_1_data;
  wire [15:0] row_value;

  // Debugger debugger_1: pin names not known
  Clock clock_1 (.out(Cl));
  Comparator comparator_1 (.a(addr), .b(8'hf2), .eq(comparator_1_eq));  // open: gt, lt
  Button UP (.out(UP_button));
  Button LEFT (.out(LEFT_button));
  Button DOWN (.out(DOWN_button));
  // CdM_8_mark5 cdm_8_mark5_1: pin names not known; wires that end beside it: Cl, data_ins_prime, memory, read_write_prime, addr, cdm_8_mark5_1_p6, cdm_8_mark5_1_p7
  Button RIGHT (.out(RIGHT_button));
  and and_1 (STOP_select, data_ins_prime, read_write_prime, comparator_1_eq);
  assign D = not_1_out ? cdm_8_mark5_1_p6 : 8'bz;  // Controlled_Buffer controlled_buffer_1
  not not_1 (not_1_out, read_write_prime);
  assign cdm_8_mark5_1_p7 = read_write_prime ? D : 8'bz;  // Controlled_Buffer controlled_buffer_2
  Button STOP (.out(STOP_out));
  Decoder decoder_1 (.out0(code), .out1(data), .sel(data_ins_prime), .en(memory));
  not not_2 (not_2_out, register_1_q[0]);
  Register #(.width(1)) register_1 (.D(not_2_out), .Q(register_1_q[0]), .clk(STOP_out));  // open: en, clr
  Counter #(.width(4), .max('hf)) X_coord (
    .load(LEFT_button), .count(or_1_out), .Q(X_coord_q), .clk(or_1_out));  // open: D, carry, clr
  or or_1 (or_1_out, RIGHT_button, LEFT_button);
  Counter #(.width(4), .max('hf)) Y_coord (
    .load(DOWN_button), .count(or_2_out), .Q(Y_coord_q), .clk(or_2_out));  // open: D, carry, clr
  or or_2 (or_2_out, UP_button, DOWN_button);
  ROM rom_1 (.addr(addr), .data(D), .sel(code));
  RAM ram_1 (.addr(addr), .data(ram_1_data), .sel(data), .clk(Cl), .ld(read_write_prime));  // open: clr
  or or_3 (or_3_out, STOP_select, CORD_select);
  assign D = STOP_select ? {{7{1'b0}}, register_1_q[0]} : 8'bz;  // Controlled_Buffer controlled_buffer_3
  Comparator comparator_2 (.a(addr), .b(8'hf5), .eq(comparator_2_eq));  // open: gt, lt
  assign ram_1_data = not_3_out ? D : 8'bz;  // Controlled_Buffer controlled_buffer_4
  not not_3 (not_3_out, or_3_out);
  assign D = CORD_select ? {Y_coord_q, X_coord_q} : 8'bz;  // Controlled_Buffer controlled_buffer_5
  and and_2 (CORD_select, data_ins_prime, read_write_prime, comparator_2_eq);
  assign {hi, column[3:1], controlled_buffer_6_out} = DISPLAY_select ? addr : 8'bz;  // Controlled_Buffer controlled_buffer_6
  Comparator comparator_3 (.a(addr), .b(8'hb0), .lt(comparator_3_lt));  // open: gt, eq
  Comparator comparator_4 (.a(addr), .b(8'hcf), .gt(comparator_4_gt));  // open: eq, lt
  Comparator comparator_5 (.a(addr), .b(8'hd0), .lt(comparator_5_lt));  // open: gt, eq
  Comparator comparator_6 (.a(addr), .b(8'hef), .gt(comparator_6_gt));  // open: eq, lt
  not not_4 (column[0], controlled_buffer_6_out[3]);
  and and_3 (and_3_out, comparator_3_lt, comparator_4_gt);
  and and_4 (and_4_out, comparator_5_lt, comparator_6_gt);
  not not_5 (lo, hi);
  or or_4 (or_4_out, and_3_out, and_4_out);
  not not_6 (not_6_out, read_write_prime);
  and and_5 (DISPLAY_select, or_4_out, data_ins_prime, not_6_out);
  and and_6 (and_6_out, DISPLAY_select, lo);
  and and_7 (and_7_out, DISPLAY_select, hi);
  Register u_lo (.en(and_6_out), .Q(row_value[7:0]));  // open: D, clk, clr
  Register u_hi (.en(and_7_out), .Q(row_value[15:8]));  // open: D, clk, clr
  DotMatrix #(.matrixcols(16), .matrixrows(16)) dotmatrix_1 ();  // open: col0, col1, col2, col3, col4, col5, col6, col7, col8, col9, col10, col11, col12, col13, col14, col15
  Register #(.width(4)) u_Column (.D(column), .en(DISPLAY_select), .Q(Column_q), .clk(Cl));  // open: clr
  Demultiplexer #(.select(4)) demultiplexer_1 (
    .out0(demultiplexer_1_out0), .out1(demultiplexer_1_out1), .out2(demultiplexer_1_out2),
    .out3(demultiplexer_1_out3), .out4(demultiplexer_1_out4), .out5(demultiplexer_1_out5),
    .out6(demultiplexer_1_out6), .out7(demultiplexer_1_out7), .out8(demultiplexer_1_out8),
    .out9(demultiplexer_1_out9), .out10(demultiplexer_1_out10), .out11(demultiplexer_1_out11),
    .out12(demultiplexer_1_out12), .out13(demultiplexer_1_out13), .out14(demultiplexer_1_out14),
    .out15(demultiplexer_1_out15), .sel(Column_q), .en(DISPLAY_select));  // open: in
  Register #(.width(16)) register_2 (.D(row_value), .en(demultiplexer_1_out0), .clk(Cl));  // open: Q, clr
  Register #(.width(16)) register_3 (.D(row_value), .en(demultiplexer_1_out1), .clk(Cl));  // open: Q, clr
  Register #(.width(16)) register_4 (.D(row_value), .en(demultiplexer_1_out2), .clk(Cl));  // open: Q, clr
  Register #(.width(16)) register_5 (.D(row_value), .en(demultiplexer_1_out3), .clk(Cl));  // open: Q, clr
  Register #(.width(16)) register_6 (.D(row_value), .en(demultiplexer_1_out4), .clk(Cl));  // open: Q, clr
  Register #(.width(16)) register_7 (.D(row_value), .en(demultiplexer_1_out5), .clk(Cl));  // open: Q, clr
  Register #(.width(16)) register_8 (.D(row_value), .en(demultiplexer_1_out6), .clk(Cl));  // open: Q, clr
  Register #(.width(16)) register_9 (.D(row_value), .en(demultiplexer_1_out7), .clk(Cl));  // open: Q, clr
  Register #(.width(16)) register_10 (.D(row_value), .en(demultiplexer_1_out8), .clk(Cl));  // open: Q, clr
  Register #(.width(16)) register_11 (.D(row_value), .en(demultiplexer_1_out9), .clk(Cl));  // open: Q, clr
  Register #(.width(16)) register_12 (.D(row_value), .en(demultiplexer_1_out10), .clk(Cl));  // open: Q, clr
  Register #(.width(16)) register_13 (.D(row_value), .en(demultiplexer_1_out11), .clk(Cl));  // open: Q, clr
  Register #(.width(16)) register_14 (.D(row_value), .en(demultiplexer_1_out12), .clk(Cl));  // open: Q, clr
  Register #(.width(16)) register_15 (.D(row_value), .en(demultiplexer_1_out13), .clk(Cl));  // open: Q, clr
  Register #(.width(16)) register_16 (.D(row_value), .en(demultiplexer_1_out14), .clk(Cl));  // open: Q, clr
  Register #(.width(16)) register_17 (.D(row_value), .en(demultiplexer_1_out15), .clk(Cl));  // open: Q, clr

  // Notes on the sheet:
  //   contents of rom_1 (hex, n*v repeats v):
  //   d0 b0 88 c1 d1 9 a4 c5 cd 0 d0 f2 b0 0 e1 19 d0 f1 d1 0 a1 d6 1a ee a d4 d1 20 89 e0 2c d0 80 0 e0
  //   29 d6 3a 98 ee 21 20 ee 1c d7 d3 f0 bf f e1 37 d2 b0 ee 39 d2 d0 d7 d6 2d 16 ba 42 a e1 46 d2 0 ee
  //   48 d2 1 d7 d7
endmodule
